// Logisim project 7seg.circ as structural Verilog: 12 circuits, main circuit main
module main (
);

  wire _0_out, c_1_a, c_1_b, c_1_c, c_1_d, c_1_e, c_1_f, c_1_g, Call_Patient_out, d_1_a, d_1_b, d_1_c, d_1_d,
       d_1_e, d_1_f, d_1_g, docnum_1_bit0, docnum_1_bit1, Doctor_1_Select_out, Doctor_2_Select_out,
       Doctor_3_Select_out, dr_1_a, dr_1_b, dr_1_c, dr_1_d, dr_1_e, dr_1_f, dr_1_g, Emergency_out,
       Mode_Selection_mode, Mode_Selection_none_registered, Mode_Selection_overflow_flag,
       n4_sec_delay_1_output, n4_sec_delay_2_output, ne_1_a, ne_1_b, ne_1_c, ne_1_d, ne_1_e, ne_1_f, ne_1_g,
       Normal_out, part1_1_a, part1_1_b, part1_1_c, part1_1_d, part1_1_e, part1_1_f, part1_1_g, part1_2_a,
       part1_2_b, part1_2_c, part1_2_d, part1_2_e, part1_2_f, part1_2_g, part2_1_a, part2_1_b, part2_1_c,
       part2_1_d, part2_1_e, part2_1_f, part2_1_g, part2_2_a, part2_2_b, part2_2_c, part2_2_d, part2_2_e,
       part2_2_f, part2_2_g, part2addon_1_i21, part2addon_1_i22, part2addon_1_i23, part2addon_1_i24,
       part2addon_2_i21, part2addon_2_i22, part2addon_2_i23, part2addon_2_i24, Patient_Confirm_out,
       Queue_Interphase_last_q_reg_1_for_em, Reset_out;
  wire [3:0] Mode_Selection_current_number_display, Queue_Interphase_last_num_popped;

  Button Normal (.out(Normal_out));
  Button Emergency (.out(Emergency_out));
  Button Patient_Confirm (.out(Patient_Confirm_out));
  Button Reset (.out(Reset_out));
  MODE_Selection Mode_Selection (
    .Normal(Normal_out), .Emergency(Emergency_out), .Patient_Confirm(Patient_Confirm_out), .Reset(Reset_out),
    .Mode(Mode_Selection_mode), .Current_Number_display(Mode_Selection_current_number_display),
    .None_Registered(Mode_Selection_none_registered), .Overflow_Flag(Mode_Selection_overflow_flag));
  _4_sec_delay u_4_sec_delay_1 (.Start(Patient_Confirm_out), .Output(n4_sec_delay_1_output));
  NE ne_1 (
    .Normal(Mode_Selection_mode), .Emergency(Emergency_out), .Enable(n4_sec_delay_1_output), .a(ne_1_a),
    .b(ne_1_b), .c(ne_1_c), .d(ne_1_d), .e(ne_1_e), .f(ne_1_f), .g(ne_1_g));
  LED Empty (.in(Mode_Selection_none_registered));
  LED Overflow (.in(Mode_Selection_overflow_flag));
  Queue_with_P_Queue Queue_Interphase (
    .Emergency_b(Emergency_out), .Patient_Confirm_b(Patient_Confirm_out), .Normal_b(Normal_out),
    .Reset(Reset_out), .last_Num_popped(Queue_Interphase_last_num_popped), .Doc_confirmed(Call_Patient_out),
    .Last_Q_reg_1_for_em(Queue_Interphase_last_q_reg_1_for_em), .Add_Q_by_1(_0_out),
    .Doc_Se1(Doctor_1_Select_out), .Doc_Se2(Doctor_2_Select_out), .Doc_Se3(Doctor_3_Select_out));  // open: Next_num, LasT_Doc_called
  Button _0 (.out(_0_out));
  _7_Segment_Display u_7_segment_display_1 (
    .g(ne_1_g), .f(ne_1_f), .a(ne_1_a), .b(ne_1_b), .e(ne_1_e), .d(ne_1_d), .c(ne_1_c));  // open: dp
  _7_Segment_Display u_7_segment_display_2 (
    .g(part1_1_g), .f(part1_1_f), .a(part1_1_a), .b(part1_1_b), .e(part1_1_e), .d(part1_1_d), .c(part1_1_c));  // open: dp
  Part1 part1_1 (
    .x1(Mode_Selection_current_number_display[3]), .x2(Mode_Selection_current_number_display[2]),
    .x3(Mode_Selection_current_number_display[1]), .x4(Mode_Selection_current_number_display[0]),
    .Enable(n4_sec_delay_1_output), .a(part1_1_a), .b(part1_1_b), .c(part1_1_c), .d(part1_1_d),
    .e(part1_1_e), .f(part1_1_f), .g(part1_1_g));
  Button Doctor_1_Select (.out(Doctor_1_Select_out));
  Button Doctor_2_Select (.out(Doctor_2_Select_out));
  Button Doctor_3_Select (.out(Doctor_3_Select_out));
  Part2addon part2addon_1 (
    .Bit3(Mode_Selection_current_number_display[3]), .Bit2(Mode_Selection_current_number_display[2]),
    .Bit1(Mode_Selection_current_number_display[1]), .Bit0(Mode_Selection_current_number_display[0]),
    .i21(part2addon_1_i21), .i22(part2addon_1_i22), .i23(part2addon_1_i23), .i24(part2addon_1_i24));
  Part2 part2_1 (
    .d0(part2addon_1_i21), .d1(part2addon_1_i22), .d2(part2addon_1_i23), .d3(part2addon_1_i24),
    .Enable(n4_sec_delay_1_output), .a(part2_1_a), .b(part2_1_b), .c(part2_1_c), .d(part2_1_d),
    .e(part2_1_e), .f(part2_1_f), .g(part2_1_g));
  _7_Segment_Display u_7_segment_display_3 (
    .g(part2_1_g), .f(part2_1_f), .a(part2_1_a), .b(part2_1_b), .e(part2_1_e), .d(part2_1_d), .c(part2_1_c));  // open: dp
  Button Call_Patient (.out(Call_Patient_out));
  _4_sec_delay u_4_sec_delay_2 (.Start(Call_Patient_out), .Output(n4_sec_delay_2_output));
  docnum docnum_1 (
    .D3(Doctor_3_Select_out), .D2(Doctor_2_Select_out), .D1(Doctor_1_Select_out), .Bit1(docnum_1_bit1),
    .Bit0(docnum_1_bit0));
  C c_1 (.Enable(n4_sec_delay_2_output), .a(c_1_a), .b(c_1_b), .c(c_1_c), .d(c_1_d), .e(c_1_e), .g(c_1_g), .f(c_1_f));
  _7_Segment_Display u_7_segment_display_4 (
    .g(c_1_g), .f(c_1_f), .a(c_1_a), .b(c_1_b), .e(c_1_e), .d(c_1_d), .c(c_1_c));  // open: dp
  _7_Segment_Display u_7_segment_display_5 (
    .g(part1_2_g), .f(part1_2_f), .a(part1_2_a), .b(part1_2_b), .e(part1_2_e), .d(part1_2_d), .c(part1_2_c));  // open: dp
  Part1 part1_2 (
    .x1(Queue_Interphase_last_num_popped[3]), .x2(Queue_Interphase_last_num_popped[2]),
    .x3(Queue_Interphase_last_num_popped[1]), .x4(Queue_Interphase_last_num_popped[0]),
    .Enable(n4_sec_delay_2_output), .a(part1_2_a), .b(part1_2_b), .c(part1_2_c), .d(part1_2_d),
    .e(part1_2_e), .f(part1_2_f), .g(part1_2_g));
  _7_Segment_Display u_7_segment_display_6 (
    .g(part2_2_g), .f(part2_2_f), .a(part2_2_a), .b(part2_2_b), .e(part2_2_e), .d(part2_2_d), .c(part2_2_c));  // open: dp
  Part2addon part2addon_2 (
    .Bit3(Queue_Interphase_last_num_popped[3]), .Bit2(Queue_Interphase_last_num_popped[2]),
    .Bit1(Queue_Interphase_last_num_popped[1]), .Bit0(Queue_Interphase_last_num_popped[0]),
    .i21(part2addon_2_i21), .i22(part2addon_2_i22), .i23(part2addon_2_i23), .i24(part2addon_2_i24));
  Part2 part2_2 (
    .d0(part2addon_2_i21), .d1(part2addon_2_i22), .d2(part2addon_2_i23), .d3(part2addon_2_i24),
    .Enable(n4_sec_delay_2_output), .a(part2_2_a), .b(part2_2_b), .c(part2_2_c), .d(part2_2_d),
    .e(part2_2_e), .f(part2_2_f), .g(part2_2_g));
  _7_Segment_Display u_7_segment_display_7 (
    .g(d_1_g), .f(d_1_f), .a(d_1_a), .b(d_1_b), .e(d_1_e), .d(d_1_d), .c(d_1_c));  // open: dp
  _7_Segment_Display u_7_segment_display_8 (
    .g(dr_1_g), .f(dr_1_f), .a(dr_1_a), .b(dr_1_b), .e(dr_1_e), .d(dr_1_d), .c(dr_1_c));  // open: dp
  D d_1 (
    .i(1'b0), .Enable(n4_sec_delay_2_output), .a(d_1_a), .b(d_1_b), .c(d_1_c), .d(d_1_d), .e(d_1_e),
    .f(d_1_f), .g(d_1_g));
  Dr dr_1 (
    .d1(docnum_1_bit1), .d2(docnum_1_bit0), .Enable(n4_sec_delay_2_output), .a(dr_1_a), .b(dr_1_b),
    .c(dr_1_c), .d(dr_1_d), .e(dr_1_e), .f(dr_1_f), .g(dr_1_g));

  // Notes on the sheet:
  //   Press 0: N
  //   Press 1: E
  //   Set Clock to 1kHz
  //   Limitations : 
  //   Each Queue has can only have 3 elements at the same time
  //   this means that only 6 people can register at a time
  //   Press 1: None
  //   Press 0: C
  //   Press 1: None
  //   Press 0: D
endmodule

module NE (
  input  Normal,
  input  Emergency,
  input  Enable,
  output a,
  output b,
  output c,
  output d,
  output e,
  output f,
  output g
);

  wire not_1_out, not_2_out, not_3_out, register_1_q;

  Register #(.width(1)) register_1 (.D(1'b1), .Q(register_1_q), .clk(Normal), .clr(Emergency));  // open: en
  not not_1 (not_1_out, register_1_q);
  not not_2 (not_2_out, not_1_out);
  not not_3 (not_3_out, not_1_out);
  and and_1 (a, 1'b1, Enable);
  and and_2 (b, not_2_out, Enable);
  and and_3 (c, not_3_out, Enable);
  and and_4 (d, not_1_out, Enable);
  and and_5 (e, 1'b1, Enable);
  and and_6 (f, 1'b1, Enable);
  and and_7 (g, not_1_out, Enable);
endmodule

module C (
  input  Enable,
  output a,
  output b,
  output c,
  output d,
  output e,
  output g,
  output f
);

  wire not_1_out, not_2_out, not_3_out, not_4_out;

  not not_1 (not_1_out, 1'b0);
  not not_2 (not_2_out, 1'b0);
  not not_3 (not_3_out, 1'b0);
  not not_4 (not_4_out, 1'b0);
  Multiplexer #(.enable("false")) multiplexer_1 (.in0(1'b0), .in1(not_1_out), .out(a), .sel(Enable));
  Multiplexer #(.enable("false")) multiplexer_2 (.in0(1'b0), .in1(not_2_out), .out(d), .sel(Enable));
  Multiplexer #(.enable("false")) multiplexer_3 (.in0(1'b0), .in1(not_3_out), .out(e), .sel(Enable));
  Multiplexer #(.enable("false")) multiplexer_4 (.in0(1'b0), .in1(not_4_out), .out(f), .sel(Enable));

  assign b = 1'b0;
  assign c = 1'b0;
  assign g = 1'b0;
endmodule

module D (
  input  i,
  input  Enable,
  output a,
  output b,
  output c,
  output d,
  output e,
  output f,
  output g
);

  wire not_1_out, not_2_out, not_3_out, not_4_out, not_5_out;

  not not_1 (not_1_out, i);
  not not_2 (not_2_out, i);
  not not_3 (not_3_out, i);
  not not_4 (not_4_out, i);
  not not_5 (not_5_out, i);
  and and_1 (b, not_1_out, Enable);
  and and_2 (c, not_2_out, Enable);
  and and_3 (d, not_3_out, Enable);
  and and_4 (e, not_4_out, Enable);
  and and_5 (g, not_5_out, Enable);

  assign a = 1'b0;
  assign f = 1'b0;
endmodule

module Part2 (
  input  d0,
  input  d1,
  input  d2,
  input  d3,
  input  Enable,
  output a,
  output b,
  output c,
  output d,
  output e,
  output f,
  output g
);

  wire and_1_out, and_2_out, and_3_out, and_4_out, and_5_out, and_6_out, and_7_out, and_8_out, and_9_out,
       and_10_out, and_11_out, and_12_out, and_13_out, and_14_out, and_15_out, and_16_out, and_17_out,
       and_18_out, and_19_out, and_20_out, and_21_out, and_22_out, and_23_out, and_24_out, and_25_out,
       and_26_out, and_27_out, and_28_out, and_29_out, and_30_out, and_31_out, not_1_out, not_2_out,
       not_3_out, not_4_out, not_5_out, not_6_out, not_7_out, not_8_out, not_9_out, not_10_out, not_11_out,
       not_12_out, not_13_out, not_14_out, not_15_out, not_16_out, not_17_out, not_18_out, not_19_out,
       not_20_out, not_21_out, not_22_out, not_23_out, not_24_out, not_25_out, not_26_out, not_27_out,
       not_28_out, not_29_out, not_30_out, not_31_out, not_32_out, not_33_out, not_34_out, not_35_out,
       not_36_out, not_37_out, not_38_out, not_39_out, not_40_out, not_41_out, not_42_out, or_1_out,
       or_2_out, or_3_out, or_4_out, or_5_out, or_6_out, or_7_out;

  not not_1 (not_1_out, d1);
  and and_1 (and_1_out, not_1_out, not_2_out);
  not not_2 (not_2_out, d3);
  not not_3 (not_3_out, d0);
  and and_2 (and_2_out, not_3_out, d2);
  and and_3 (and_3_out, d1, d3);
  not not_4 (not_4_out, d1);
  and and_4 (and_4_out, d0, not_4_out, not_5_out);
  not not_5 (not_5_out, d2);
  not not_6 (not_6_out, d1);
  and and_5 (and_5_out, not_6_out, not_7_out);
  not not_7 (not_7_out, d3);
  not not_8 (not_8_out, d2);
  and and_6 (and_6_out, not_8_out, not_9_out);
  not not_9 (not_9_out, d3);
  not not_10 (not_10_out, d0);
  and and_7 (and_7_out, not_10_out, d2, d3);
  and and_8 (and_8_out, d0, not_11_out);
  not not_11 (not_11_out, d2);
  and and_9 (and_9_out, d0, not_12_out);
  not not_12 (not_12_out, d3);
  not not_13 (not_13_out, d2);
  and and_10 (and_10_out, not_13_out, not_14_out);
  not not_14 (not_14_out, d3);
  not not_15 (not_15_out, d0);
  and and_11 (and_11_out, not_15_out, d2, d3);
  and and_12 (and_12_out, d0, not_16_out);
  not not_16 (not_16_out, d2);
  and and_13 (and_13_out, d0, not_17_out);
  not not_17 (not_17_out, d3);
  not not_18 (not_18_out, d1);
  and and_14 (and_14_out, not_18_out, not_19_out);
  not not_19 (not_19_out, d3);
  not not_20 (not_20_out, d0);
  and and_15 (and_15_out, not_20_out, not_21_out, d2);
  not not_21 (not_21_out, d1);
  not not_22 (not_22_out, d0);
  and and_16 (and_16_out, not_22_out, d2, not_23_out);
  not not_23 (not_23_out, d3);
  not not_24 (not_24_out, d2);
  and and_17 (and_17_out, d1, not_24_out, d3);
  and and_18 (and_18_out, d0, d1, d3);
  not not_25 (not_25_out, d0);
  not not_26 (not_26_out, d1);
  and and_19 (and_19_out, not_25_out, not_26_out, not_27_out);
  not not_27 (not_27_out, d2);
  not not_28 (not_28_out, d1);
  and and_20 (and_20_out, not_28_out, not_29_out);
  not not_29 (not_29_out, d3);
  not not_30 (not_30_out, d0);
  and and_21 (and_21_out, not_30_out, d2, not_31_out);
  not not_31 (not_31_out, d3);
  not not_32 (not_32_out, d1);
  and and_22 (and_22_out, d0, not_32_out, d2);
  not not_33 (not_33_out, d0);
  and and_23 (and_23_out, not_33_out, not_34_out);
  not not_34 (not_34_out, d2);
  not not_35 (not_35_out, d2);
  and and_24 (and_24_out, not_35_out, not_36_out);
  not not_36 (not_36_out, d3);
  and and_25 (and_25_out, d1, d2);
  and and_26 (and_26_out, d0, not_37_out);
  not not_37 (not_37_out, d1);
  not not_38 (not_38_out, d0);
  not not_39 (not_39_out, d1);
  and and_27 (and_27_out, not_38_out, not_39_out, d2);
  and and_28 (and_28_out, d1, not_40_out);
  not not_40 (not_40_out, d2);
  and and_29 (and_29_out, d1, not_41_out);
  not not_41 (not_41_out, d3);
  and and_30 (and_30_out, d0, not_42_out);
  not not_42 (not_42_out, d2);
  and and_31 (and_31_out, d0, d1);
  or or_1 (or_1_out, and_1_out, and_2_out, and_3_out, and_4_out);
  or or_2 (or_2_out, and_5_out, and_6_out, and_7_out, and_8_out, and_9_out);
  or or_3 (or_3_out, and_10_out, and_11_out, d1, and_12_out, and_13_out);
  or or_4 (or_4_out, and_14_out, and_15_out, and_16_out, and_17_out, and_18_out);
  or or_5 (or_5_out, and_19_out, and_20_out, and_21_out, and_22_out);
  or or_6 (or_6_out, and_23_out, and_24_out, and_25_out, and_26_out);
  or or_7 (or_7_out, and_27_out, and_28_out, and_29_out, and_30_out, and_31_out);
  Multiplexer #(.enable("false")) multiplexer_1 (.in0(1'b0), .in1(or_6_out), .out(f), .sel(Enable));
  Multiplexer #(.enable("false")) multiplexer_2 (.in0(1'b0), .in1(or_7_out), .out(g), .sel(Enable));
  Multiplexer #(.enable("false")) multiplexer_3 (.in0(1'b0), .in1(or_1_out), .out(a), .sel(Enable));
  Multiplexer #(.enable("false")) multiplexer_4 (.in0(1'b0), .in1(or_2_out), .out(b), .sel(Enable));
  Multiplexer #(.enable("false")) multiplexer_5 (.in0(1'b0), .in1(or_3_out), .out(c), .sel(Enable));
  Multiplexer #(.enable("false")) multiplexer_6 (.in0(1'b0), .in1(or_4_out), .out(d), .sel(Enable));
  Multiplexer #(.enable("false")) multiplexer_7 (.in0(1'b0), .in1(or_5_out), .out(e), .sel(Enable));
endmodule

module Part2addon (
  input  Bit3,
  input  Bit2,
  input  Bit1,
  input  Bit0,
  output i21,
  output i22,
  output i23,
  output i24
);

  wire and_2_out, and_3_out, and_4_out, and_5_out, not_1_out, not_2_out, not_3_out, not_4_out, not_5_out;

  not not_1 (not_1_out, Bit2);
  and and_1 (i21, Bit3, not_1_out, not_2_out);
  not not_2 (not_2_out, Bit1);
  not not_3 (not_3_out, Bit3);
  and and_2 (and_2_out, not_3_out, Bit2);
  and and_3 (and_3_out, Bit2, Bit1);
  not not_4 (not_4_out, Bit3);
  and and_4 (and_4_out, not_4_out, Bit1);
  and and_5 (and_5_out, Bit3, Bit2, not_5_out);
  not not_5 (not_5_out, Bit1);
  or or_1 (i22, and_2_out, and_3_out);
  or or_2 (i23, and_4_out, and_5_out);

  assign i24 = Bit0;
endmodule

module Part1 (
  input  x1,
  input  x2,
  input  x3,
  input  x4,
  input  Enable,
  output a,
  output b,
  output c,
  output d,
  output e,
  output f,
  output g
);

  wire and_1_out, and_2_out, and_3_out, and_4_out, not_1_out, not_2_out, not_3_out, not_4_out, not_5_out,
       not_6_out, not_7_out, not_8_out, not_9_out, not_10_out, not_11_out, not_12_out, or_1_out, or_2_out,
       or_3_out, or_4_out;

  not not_1 (not_1_out, x2);
  not not_2 (not_2_out, x3);
  not not_3 (not_3_out, x2);
  not not_4 (not_4_out, x3);
  not not_5 (not_5_out, x2);
  not not_6 (not_6_out, x3);
  not not_7 (not_7_out, x2);
  not not_8 (not_8_out, x3);
  not not_9 (not_9_out, x1);
  and and_1 (and_1_out, not_1_out, not_2_out);
  not not_10 (not_10_out, x1);
  and and_2 (and_2_out, not_3_out, not_4_out);
  not not_11 (not_11_out, x1);
  and and_3 (and_3_out, not_5_out, not_6_out);
  not not_12 (not_12_out, x1);
  and and_4 (and_4_out, not_7_out, not_8_out);
  or or_1 (or_1_out, not_9_out, and_1_out);
  or or_2 (or_2_out, not_10_out, and_2_out);
  or or_3 (or_3_out, not_11_out, and_3_out);
  or or_4 (or_4_out, not_12_out, and_4_out);
  Multiplexer #(.enable("false")) multiplexer_1 (.in1(or_1_out), .out(a), .sel(Enable));  // open: in0
  Multiplexer #(.enable("false")) multiplexer_2 (.in1(or_2_out), .out(b), .sel(Enable));  // open: in0
  Multiplexer #(.enable("false")) multiplexer_3 (.in1(or_3_out), .out(c), .sel(Enable));  // open: in0
  Multiplexer #(.enable("false")) multiplexer_4 (.in1(or_4_out), .out(d), .sel(Enable));  // open: in0
  Multiplexer #(.enable("false")) multiplexer_5 (.in1(1'b1), .out(e), .sel(Enable));  // open: in0
  Multiplexer #(.enable("false")) multiplexer_6 (.in1(1'b1), .out(f), .sel(Enable));  // open: in0
  Multiplexer #(.enable("false")) multiplexer_7 (.in1(1'b0), .out(g), .sel(Enable));  // open: in0
endmodule

module Dr (
  input  d1,
  input  d2,
  input  Enable,
  output a,
  output b,
  output c,
  output d,
  output e,
  output f,
  output g
);

  wire and_1_out, and_2_out, not_1_out, not_2_out, not_3_out, not_4_out, not_5_out, not_6_out, not_7_out,
       not_8_out, or_1_out, or_2_out, or_3_out, or_4_out, or_5_out;

  not not_1 (not_1_out, d2);
  not not_2 (not_2_out, d2);
  not not_3 (not_3_out, d1);
  not not_4 (not_4_out, d2);
  not not_5 (not_5_out, d2);
  not not_6 (not_6_out, d1);
  not not_7 (not_7_out, d2);
  not not_8 (not_8_out, d1);
  or or_1 (or_1_out, not_1_out, d1);
  or or_2 (or_2_out, not_2_out, d1);
  and and_1 (and_1_out, not_3_out, not_4_out);
  and and_2 (and_2_out, d1, d2);
  or or_3 (or_3_out, not_5_out, d1);
  or or_4 (or_4_out, not_6_out, not_7_out);
  or or_5 (or_5_out, and_1_out, and_2_out);
  Multiplexer #(.enable("false")) multiplexer_1 (.in0(1'b0), .in1(d1), .out(g), .sel(Enable));
  Multiplexer #(.enable("false")) multiplexer_2 (.in0(1'b0), .in1(or_1_out), .out(a), .sel(Enable));
  Multiplexer #(.enable("false")) multiplexer_3 (.in0(1'b0), .in1(or_2_out), .out(b), .sel(Enable));
  Multiplexer #(.enable("false")) multiplexer_4 (.in0(1'b0), .in1(or_5_out), .out(c), .sel(Enable));
  Multiplexer #(.enable("false")) multiplexer_5 (.in0(1'b0), .in1(not_8_out), .out(f), .sel(Enable));
  Multiplexer #(.enable("false")) multiplexer_6 (.in0(1'b0), .in1(or_3_out), .out(d), .sel(Enable));
  Multiplexer #(.enable("false")) multiplexer_7 (.in0(1'b0), .in1(or_4_out), .out(e), .sel(Enable));
endmodule

module Call_7seg (
  input  P_Bit3,
  input  D_Bit1,
  input  P_Bit2,
  input  P_Bit1,
  input  D_Bit0,
  input  P_Bit0
);

  wire c_1_a, c_1_b, c_1_c, c_1_d, c_1_e, c_1_f, c_1_g, d_1_a, d_1_b, d_1_c, d_1_d, d_1_e, d_1_f, d_1_g,
       dr_1_a, dr_1_b, dr_1_c, dr_1_d, dr_1_e, dr_1_f, dr_1_g, part1_1_a, part1_1_b, part1_1_c, part1_1_d,
       part1_1_e, part1_1_f, part1_1_g, part2_1_a, part2_1_b, part2_1_c, part2_1_d, part2_1_e, part2_1_f,
       part2_1_g, part2addon_1_i21, part2addon_1_i22, part2addon_1_i23, part2addon_1_i24;

  C c_1 (.Enable(1'b0), .a(c_1_a), .b(c_1_b), .c(c_1_c), .d(c_1_d), .e(c_1_e), .g(c_1_g), .f(c_1_f));
  _7_Segment_Display u_7_segment_display_1 (
    .g(c_1_f), .f(c_1_g), .a(c_1_a), .b(c_1_b), .e(c_1_e), .d(c_1_d), .c(c_1_c));  // open: dp
  Part1 part1_1 (
    .x1(P_Bit3), .x2(P_Bit2), .x3(P_Bit1), .x4(P_Bit0), .a(part1_1_a), .b(part1_1_b), .c(part1_1_c),
    .d(part1_1_d), .e(part1_1_e), .f(part1_1_f), .g(part1_1_g));  // open: Enable
  _7_Segment_Display u_7_segment_display_2 (
    .g(part1_1_g), .f(part1_1_f), .a(part1_1_a), .b(part1_1_b), .e(part1_1_e), .d(part1_1_d), .c(part1_1_c));  // open: dp
  Part2addon part2addon_1 (
    .Bit3(P_Bit3), .Bit2(P_Bit2), .Bit1(P_Bit1), .Bit0(P_Bit0), .i21(part2addon_1_i21),
    .i22(part2addon_1_i22), .i23(part2addon_1_i23), .i24(part2addon_1_i24));
  Part2 part2_1 (
    .d0(part2addon_1_i21), .d1(part2addon_1_i22), .d2(part2addon_1_i23), .d3(part2addon_1_i24),
    .a(part2_1_a), .b(part2_1_b), .c(part2_1_c), .d(part2_1_d), .e(part2_1_e), .f(part2_1_f), .g(part2_1_g));  // open: Enable
  _7_Segment_Display u_7_segment_display_3 (
    .g(part2_1_g), .f(part2_1_f), .a(part2_1_a), .b(part2_1_b), .e(part2_1_e), .d(part2_1_d), .c(part2_1_c));  // open: dp
  _7_Segment_Display u_7_segment_display_4 (
    .g(d_1_g), .f(d_1_f), .a(d_1_a), .b(d_1_b), .e(d_1_e), .d(d_1_d), .c(d_1_c));  // open: dp
  D d_1 (.Enable(1'b0), .a(d_1_a), .b(d_1_b), .c(d_1_c), .d(d_1_d), .e(d_1_e), .f(d_1_f), .g(d_1_g));  // open: i
  Dr dr_1 (
    .d1(D_Bit1), .d2(D_Bit0), .a(dr_1_a), .b(dr_1_b), .c(dr_1_c), .d(dr_1_d), .e(dr_1_e), .f(dr_1_f),
    .g(dr_1_g));  // open: Enable
  _7_Segment_Display u_7_segment_display_5 (
    .g(dr_1_g), .f(dr_1_f), .a(dr_1_a), .b(dr_1_b), .e(dr_1_e), .d(dr_1_d), .c(dr_1_c));  // open: dp

  // Notes on the sheet:
  //   Press 1: None
  //   Press 0: C
  //   Press 0: D
  //   Press 1: None
endmodule

module Register_7_seg (
  input  Bit3,
  input  Bit2,
  input  Bit1,
  input  Bit0,
  input  Emergency
);

  wire ne_1_a, ne_1_b, ne_1_c, ne_1_d, ne_1_e, ne_1_f, ne_1_g, part1_1_a, part1_1_b, part1_1_c, part1_1_d,
       part1_1_e, part1_1_f, part1_1_g, part2_1_a, part2_1_b, part2_1_c, part2_1_d, part2_1_e, part2_1_f,
       part2_1_g, part2addon_1_i21, part2addon_1_i22, part2addon_1_i23, part2addon_1_i24;

  NE ne_1 (
    .Emergency(Emergency), .a(ne_1_a), .b(ne_1_b), .c(ne_1_c), .d(ne_1_d), .e(ne_1_e), .f(ne_1_f), .g(ne_1_g));  // open: Normal, Enable
  _7_Segment_Display u_7_segment_display_1 (
    .g(part1_1_g), .f(part1_1_f), .a(part1_1_a), .b(part1_1_b), .e(part1_1_e), .d(part1_1_d), .c(part1_1_c));  // open: dp
  _7_Segment_Display u_7_segment_display_2 (
    .g(ne_1_g), .f(ne_1_f), .a(ne_1_a), .b(ne_1_b), .e(ne_1_e), .d(ne_1_d), .c(ne_1_c));  // open: dp
  Part1 part1_1 (
    .x1(Bit3), .x2(Bit2), .x3(Bit1), .x4(Bit0), .a(part1_1_a), .b(part1_1_b), .c(part1_1_c), .d(part1_1_d),
    .e(part1_1_e), .f(part1_1_f), .g(part1_1_g));  // open: Enable
  Part2addon part2addon_1 (
    .Bit3(Bit3), .Bit2(Bit2), .Bit1(Bit1), .Bit0(Bit0), .i21(part2addon_1_i21), .i22(part2addon_1_i22),
    .i23(part2addon_1_i23), .i24(part2addon_1_i24));
  Part2 part2_1 (
    .d0(part2addon_1_i21), .d1(part2addon_1_i22), .d2(part2addon_1_i23), .d3(part2addon_1_i24),
    .a(part2_1_a), .b(part2_1_b), .c(part2_1_c), .d(part2_1_d), .e(part2_1_e), .f(part2_1_f), .g(part2_1_g));  // open: Enable
  _7_Segment_Display u_7_segment_display_3 (
    .g(part2_1_g), .f(part2_1_f), .a(part2_1_a), .b(part2_1_b), .e(part2_1_e), .d(part2_1_d), .c(part2_1_c));  // open: dp

  // Notes on the sheet:
  //   Press 0: N
  //   Press 1: E
endmodule

module MODE_Selection (
  input  Normal,
  input  Emergency,
  input  Patient_Confirm,
  input  Reset,
  output Mode,
  output [3:0] Current_Number_display,
  output None_Registered,
  output Overflow_Flag
);

  wire and_1_out, d_ff_1_q, or_1_out;
  wire [3:0] counter_1_q;

  or or_1 (or_1_out, Normal, Emergency);
  D_Flip_Flop d_ff_1 (.clk(or_1_out), .D(or_1_out), .Q(d_ff_1_q), .reset(Patient_Confirm));  // open: Qn, preset, en
  Counter #(.width(4), .max('hf)) counter_1 (
    .count(and_1_out), .Q(counter_1_q), .carry(Overflow_Flag), .clk(and_1_out), .clr(Reset));  // open: load, D
  and and_1 (and_1_out, d_ff_1_q, Patient_Confirm);
  Subtractor #(.width(4)) subtractor_1 (
    .a(counter_1_q), .b(4'b0001), .out(Current_Number_display), .bout(None_Registered));  // open: bin

  assign Mode = Normal;

  // Notes on the sheet:
  //   1 is normal reg
endmodule

module docnum (
  input  D3,
  input  D2,
  input  D1,
  output Bit1,
  output Bit0
);

  wire and_1_out, and_2_out, and_3_out, and_4_out, not_1_out, not_2_out, not_3_out, not_4_out, not_5_out,
       not_6_out, not_7_out, not_8_out, or_1_out;
  wire [1:0] or_3_out;

  or or_1 (or_1_out, D1, D2, D3);
  not not_1 (not_1_out, D3);
  not not_2 (not_2_out, D1);
  not not_3 (not_3_out, D2);
  not not_4 (not_4_out, D1);
  not not_5 (not_5_out, D3);
  not not_6 (not_6_out, D2);
  not not_7 (not_7_out, D2);
  not not_8 (not_8_out, D1);
  and and_1 (and_1_out, not_1_out, D2, not_2_out);
  and and_2 (and_2_out, D3, not_3_out, not_4_out);
  and and_3 (and_3_out, not_5_out, not_6_out, D1);
  and and_4 (and_4_out, D3, not_7_out, not_8_out);
  or or_2 (or_3_out[1], and_1_out, and_2_out);
  or or_3 (or_3_out[0], and_3_out, and_4_out);
  Register #(.width(2), .trigger("high")) register_1 (.D(or_3_out), .Q({Bit1, Bit0}), .clk(or_1_out));  // open: en, clr
endmodule
