// Logisim project Queue finished.circ as structural Verilog: 7 circuits, main circuit main
module main (
  output [2:0] Output,
  output out_2,
  output [2:0] out_3,
  output [1:0] out_4
);

  wire D2_out, D3_out, Emergency_out, INC_out, Normal_out, P_confirm_out, queue_with_p_queue_1_p4,
       queue_with_p_queue_1_p6, queue_with_p_queue_1_p10;

  Button Emergency (.out(Emergency_out));
  Button Normal (.out(Normal_out));
  Button P_confirm (.out(P_confirm_out));
  Button D2 (.out(D2_out));
  Button D3 (.out(D3_out));
  Button INC (.out(INC_out));
  // Queue_with_P_Queue queue_with_p_queue_1: pin names not known; wires that end beside it: Emergency_out, P_confirm_out, Normal_out, queue_with_p_queue_1_p4, Output, queue_with_p_queue_1_p6, out_2, INC_out, out_3, queue_with_p_queue_1_p10, D2_out, D3_out, out_4
  Button Reset (.out(queue_with_p_queue_1_p4));
  Button D1 (.out(queue_with_p_queue_1_p10));
  Button D_confirm (.out(queue_with_p_queue_1_p6));
endmodule

module oneTonine (
  input  d3,
  input  d2,
  input  d1,
  input  d0,
  output a,
  output b,
  output c,
  output d,
  output e,
  output f,
  output g
);

  wire and_1_out, and_2_out, and_3_out, and_4_out, and_5_out, and_6_out, and_7_out, and_8_out, and_9_out,
       and_10_out, and_11_out, and_12_out, and_13_out, and_14_out, and_15_out, and_16_out, and_17_out,
       and_18_out, not_1_out, not_2_out, not_3_out, not_4_out, not_5_out, not_6_out, not_7_out, not_8_out,
       not_9_out, not_10_out, not_11_out, not_12_out, not_13_out, not_14_out, not_15_out, not_16_out,
       not_17_out, not_18_out, not_19_out, not_20_out, not_21_out, not_22_out, not_23_out, not_24_out;

  not not_1 (not_1_out, d2);
  and and_1 (and_1_out, not_1_out, not_2_out);
  not not_2 (not_2_out, d0);
  and and_2 (and_2_out, d2, d0);
  not not_3 (not_3_out, d2);
  and and_3 (and_3_out, not_3_out, not_4_out);
  not not_4 (not_4_out, d0);
  not not_5 (not_5_out, d1);
  and and_4 (and_4_out, not_5_out, not_6_out);
  not not_6 (not_6_out, d0);
  and and_5 (and_5_out, d1, d0);
  not not_7 (not_7_out, d1);
  and and_6 (and_6_out, not_7_out, not_8_out);
  not not_8 (not_8_out, d0);
  and and_7 (and_7_out, d1, d0);
  not not_9 (not_9_out, d2);
  and and_8 (and_8_out, not_9_out, not_10_out);
  not not_10 (not_10_out, d0);
  not not_11 (not_11_out, d2);
  and and_9 (and_9_out, not_11_out, d1);
  and and_10 (and_10_out, d1, not_12_out);
  not not_12 (not_12_out, d0);
  not not_13 (not_13_out, d1);
  and and_11 (and_11_out, d2, not_13_out, d0);
  not not_14 (not_14_out, d3);
  not not_15 (not_15_out, d2);
  and and_12 (and_12_out, not_14_out, not_15_out, not_16_out);
  not not_16 (not_16_out, d1);
  not not_17 (not_17_out, d2);
  and and_13 (and_13_out, not_17_out, not_18_out);
  not not_18 (not_18_out, d0);
  and and_14 (and_14_out, d1, not_19_out);
  not not_19 (not_19_out, d0);
  not not_20 (not_20_out, d1);
  and and_15 (and_15_out, d2, not_21_out);
  not not_21 (not_21_out, d0);
  not not_22 (not_22_out, d2);
  and and_16 (and_16_out, not_22_out, d1);
  and and_17 (and_17_out, d2, not_23_out);
  not not_23 (not_23_out, d1);
  and and_18 (and_18_out, d2, not_24_out);
  not not_24 (not_24_out, d0);
  or or_1 (a, and_1_out, d1, and_2_out, d3);
  or or_2 (b, and_3_out, and_4_out, and_5_out, d3);
  or or_3 (c, and_6_out, and_7_out, d2, d3);
  or or_4 (d, and_8_out, and_9_out, and_10_out, and_11_out, d3);
  or or_5 (e, and_12_out, and_13_out, and_14_out);
  or or_6 (f, not_20_out, and_15_out);
  or or_7 (g, and_16_out, and_17_out, and_18_out, d3);
endmodule

module _4_3 (
  input  d3,
  input  d2,
  input  d1,
  input  d0,
  output a,
  output b,
  output c
);

  wire and_1_out, and_2_out, and_4_out, and_5_out, and_6_out, and_7_out, and_8_out, not_1_out, not_2_out,
       not_3_out, not_4_out, not_5_out, not_6_out, not_7_out, not_8_out;

  and and_1 (and_1_out, d1, not_1_out);
  not not_1 (not_1_out, d0);
  and and_2 (and_2_out, d2, not_2_out);
  not not_2 (not_2_out, d1);
  not not_3 (not_3_out, d3);
  and and_3 (b, not_3_out, d1, d0);
  not not_4 (not_4_out, d1);
  and and_4 (and_4_out, not_4_out, d0);
  and and_5 (and_5_out, d1, not_5_out);
  not not_5 (not_5_out, d0);
  not not_6 (not_6_out, d3);
  and and_6 (and_6_out, not_6_out, d2);
  and and_7 (and_7_out, d3, not_7_out);
  not not_7 (not_7_out, d2);
  and and_8 (and_8_out, d3, not_8_out);
  not not_8 (not_8_out, d1);
  or or_1 (a, and_1_out, and_2_out, d3);
  or or_2 (c, and_4_out, and_5_out, and_6_out, and_7_out, and_8_out);
endmodule

module _3_4 (
  input  d2,
  input  d1,
  input  d0,
  output a,
  output b,
  output c,
  output d
);

  wire not_1_out, not_2_out, not_3_out, not_4_out, not_5_out, not_6_out, not_7_out, not_8_out;

  not not_1 (not_1_out, d2);
  not not_2 (not_2_out, d2);
  not not_3 (not_3_out, d0);
  not not_4 (not_4_out, d2);
  not not_5 (not_5_out, d1);
  not not_6 (not_6_out, d2);
  not not_7 (not_7_out, d1);
  not not_8 (not_8_out, d0);
  and and_1 (a, not_1_out, d1, d0);
  and and_2 (b, not_2_out, d1, not_3_out);
  and and_3 (c, not_4_out, not_5_out, d0);
  and and_4 (d, not_6_out, not_7_out, not_8_out);
endmodule

module Queue (
  input  PC,
  input  DS,
  input  [3:0] Num_input,
  input  DCP,
  input  PSQ,
  input  Reset,
  output [1:0] Index,
  output [3:0] Popout
);

  wire and_1_out, and_2_out, and_3_out, and_4_out, button_1_out, button_2_out, clock_1_out, d_ff_1_q,
       d_ff_2_q, multiplexer_1_out, n3_4_1_a, n3_4_1_b, n3_4_1_c, n3_4_1_d, or_1_out, or_2_out, or_3_out,
       or_4_out, or_5_out, or_6_out, or_7_out, or_8_out, or_9_out;
  wire [1:0] adder_1_out, bit_extender_1_out, multiplexer_2_out, subtractor_1_out;
  wire [3:0] bit_extender_2_out, multiplexer_3_out, multiplexer_4_out, multiplexer_5_out, multiplexer_6_out,
       register_2_q, register_3_q, register_4_q, register_5_q;

  assign bit_extender_1_out = {{1{1'b0}}, 1'b1};  // Bit_Extender bit_extender_1
  Button button_1 (.out(button_1_out));
  Clock clock_1 (.out(clock_1_out));
  Adder #(.width(2)) adder_1 (.a(Index), .b(bit_extender_1_out), .out(adder_1_out));  // open: cin, cout
  Subtractor #(.width(2)) subtractor_1 (.a(Index), .b(bit_extender_1_out), .out(subtractor_1_out));  // open: bin, bout
  or or_1 (or_1_out, DS, or_2_out);
  or or_2 (or_2_out, button_1_out, PSQ);
  Multiplexer #(.disabled(0), .enable("false")) multiplexer_1 (
    .in0(1'b0), .in1(clock_1_out), .out(multiplexer_1_out), .sel(PSQ));
  D_Flip_Flop d_ff_1 (.clk(or_1_out), .D(or_2_out), .Q(d_ff_1_q));  // open: Qn, preset, en, reset
  or or_3 (or_3_out, DS, multiplexer_1_out);
  Multiplexer #(.width(2)) multiplexer_2 (
    .in0(subtractor_1_out), .in1(adder_1_out), .out(multiplexer_2_out), .sel(d_ff_1_q));  // open: en
  Register #(.width(2)) register_1 (.D(multiplexer_2_out), .Q(Index), .clk(or_4_out));  // open: en, clr
  or or_4 (or_4_out, or_9_out, PC);
  assign bit_extender_2_out = {{3{1'b0}}, 1'b0};  // Bit_Extender bit_extender_2
  Multiplexer #(.width(4)) multiplexer_3 (
    .in0(bit_extender_2_out), .in1(Num_input), .out(multiplexer_3_out), .sel(d_ff_2_q));  // open: en
  D_Flip_Flop d_ff_2 (.clk(or_3_out), .D(multiplexer_1_out), .Q(d_ff_2_q));  // open: Qn, preset, en, reset
  Register #(.width(4)) register_2 (.D(multiplexer_3_out), .en(1'b1), .Q(register_2_q), .clk(or_5_out), .clr(Reset));
  or or_5 (or_5_out, and_1_out, DCP);
  and and_1 (and_1_out, multiplexer_1_out, n3_4_1_a);
  Multiplexer #(.width(4)) multiplexer_4 (
    .in0(register_2_q), .in1(Num_input), .out(multiplexer_4_out), .sel(d_ff_2_q));  // open: en
  and and_2 (and_2_out, multiplexer_1_out, n3_4_1_c);
  _3_4 u_3_4_1 (.d2(1'b0), .d1(Index[0]), .d0(Index[1]), .a(n3_4_1_a), .b(n3_4_1_b), .c(n3_4_1_c), .d(n3_4_1_d));
  Register #(.width(4)) register_3 (.D(multiplexer_4_out), .en(1'b1), .Q(register_3_q), .clk(or_6_out), .clr(Reset));
  or or_6 (or_6_out, and_2_out, DCP);
  Register #(.width(4)) register_4 (.D(multiplexer_5_out), .en(1'b1), .Q(register_4_q), .clk(or_7_out), .clr(Reset));
  Multiplexer #(.width(4)) multiplexer_5 (
    .in0(register_3_q), .in1(Num_input), .out(multiplexer_5_out), .sel(d_ff_2_q));  // open: en
  or or_7 (or_7_out, and_3_out, DCP);
  and and_3 (and_3_out, multiplexer_1_out, n3_4_1_b);
  Multiplexer #(.width(4)) multiplexer_6 (
    .in0(register_4_q), .in1(Num_input), .out(multiplexer_6_out), .sel(d_ff_2_q));  // open: en
  and and_4 (and_4_out, multiplexer_1_out, n3_4_1_d);
  Register #(.width(4)) register_5 (.D(multiplexer_6_out), .en(1'b1), .Q(register_5_q), .clk(or_8_out), .clr(Reset));
  or or_8 (or_8_out, and_4_out, DCP);
  or or_9 (or_9_out, button_2_out, DCP);
  Register #(.width(4)) register_6 (.D(register_5_q), .en(1'b1), .Q(Popout), .clk(DCP), .clr(Reset));
  Button button_2 (.out(button_2_out));

  // Notes on the sheet:
  //   Keep both 01
  //   Doc Select
  //   Patient Select
  //   Patient queue
  //   Patient comfirm
  //   Doctor confirm
  //   Doctor confirm
  //   And Pop
  //   2
  //   1
endmodule

module Queue_with_P_Queue (
  input  Emergency_b,
  input  Doc_confirmed,
  input  Patient_Confirm_b,
  input  Add_Q_by_1,
  input  Doc_Se1,
  input  Doc_Se2,
  input  Normal_b,
  input  Doc_Se3,
  input  Reset,
  output [3:0] last_Num_popped,
  output Last_Q_reg_1_for_em,
  output [3:0] Next_num,
  output [1:0] LasT_Doc_called
);

  wire and_1_out, and_2_out, and_3_out, and_4_out, and_5_out, d_ff_1_q, d_ff_2_q, d_ff_4_q, d_ff_5_q,
       d_ff_6_q, d_ff_7_q, demultiplexer_1_out0, demultiplexer_1_out1, demultiplexer_2_out0,
       demultiplexer_2_out1, n4_2_1_x, n4_2_1_y, nand_1_out, nand_2_out, or_1_out, or_2_out, or_3_out,
       or_4_out, or_5_out, or_6_out, or_7_out, or_8_out, or_9_out;
  wire [1:0] queue_1_index, queue_2_index;
  wire [3:0] adder_1_out, bit_extender_1_out, queue_1_popout, queue_2_popout;

  assign bit_extender_1_out = {{3{1'b0}}, 1'b1};  // Bit_Extender bit_extender_1
  and and_1 (and_1_out, d_ff_2_q, Patient_Confirm_b);
  Adder #(.width(4)) adder_1 (.a(Next_num), .b(bit_extender_1_out), .out(adder_1_out));  // open: cin, cout
  or or_1 (or_1_out, Emergency_b, Normal_b);
  D_Flip_Flop d_ff_1 (.clk(or_1_out), .D(Emergency_b), .Q(d_ff_1_q));  // open: Qn, preset, en, reset
  D_Flip_Flop d_ff_2 (.clk(or_1_out), .D(or_1_out), .Q(d_ff_2_q), .reset(and_1_out));  // open: Qn, preset, en
  Register #(.width(4)) register_1 (.D(adder_1_out), .Q(Next_num), .clk(or_2_out), .clr(Reset));  // open: en
  or or_2 (or_2_out, or_3_out, Add_Q_by_1);
  Demultiplexer #(.enable("false")) demultiplexer_1 (
    .out0(demultiplexer_1_out0), .out1(demultiplexer_1_out1), .in(and_1_out), .sel(d_ff_1_q));
  and and_2 (and_2_out, nand_1_out, demultiplexer_1_out1);
  or or_3 (or_3_out, and_2_out, and_3_out);
  and and_3 (and_3_out, nand_2_out, demultiplexer_1_out0);
  nand nand_1 (nand_1_out, queue_1_index[1], queue_1_index[0]);
  Queue queue_1 (
    .DS(or_9_out), .Num_input(Next_num), .PSQ(Emergency_b), .Reset(Reset), .Index(queue_1_index),
    .PC(and_2_out), .DCP(demultiplexer_2_out1), .Popout(queue_1_popout));
  nand nand_2 (nand_2_out, queue_2_index[1], queue_2_index[0]);
  Queue queue_2 (
    .DS(or_9_out), .Num_input(Next_num), .PSQ(Normal_b), .Reset(Reset), .Index(queue_2_index),
    .PC(and_3_out), .DCP(and_4_out), .Popout(queue_2_popout));
  and and_4 (and_4_out, demultiplexer_2_out0, or_6_out);
  or or_4 (or_4_out, and_2_out, and_3_out);
  D_Flip_Flop d_ff_3 (.clk(or_4_out), .D(d_ff_1_q), .Q(Last_Q_reg_1_for_em));  // open: Qn, preset, en, reset
  or or_5 (or_5_out, queue_1_index[0], queue_1_index[1]);
  or or_6 (or_6_out, queue_2_index[0], queue_2_index[1]);
  Demultiplexer #(.enable("false")) demultiplexer_2 (
    .out0(demultiplexer_2_out0), .out1(demultiplexer_2_out1), .in(and_5_out), .sel(d_ff_4_q));
  D_Flip_Flop d_ff_4 (.clk(or_9_out), .D(or_5_out), .Q(d_ff_4_q));  // open: Qn, preset, en, reset
  Multiplexer #(.width(4), .enable("false")) multiplexer_1 (
    .in0(queue_2_popout), .in1(queue_1_popout), .out(last_Num_popped), .sel(d_ff_4_q));
  and and_5 (and_5_out, Doc_confirmed, d_ff_5_q);
  or or_7 (or_7_out, and_5_out, or_9_out);
  _4_2 u_4_2_1 (.a(Doc_Se1), .b(Doc_Se2), .c(Doc_Se3), .d(1'b0), .x(n4_2_1_x), .y(n4_2_1_y));
  or or_8 (or_8_out, n4_2_1_y, n4_2_1_x);
  or or_9 (or_9_out, Doc_Se1, Doc_Se2, Doc_Se3);
  D_Flip_Flop d_ff_5 (.clk(or_7_out), .D(or_9_out), .Q(d_ff_5_q));  // open: Qn, preset, en, reset
  D_Flip_Flop d_ff_6 (.clk(or_8_out), .D(n4_2_1_x), .Q(d_ff_6_q));  // open: Qn, preset, en, reset
  D_Flip_Flop d_ff_7 (.clk(or_8_out), .D(n4_2_1_y), .Q(d_ff_7_q));  // open: Qn, preset, en, reset
  assign LasT_Doc_called = {{1{d_ff_6_q}}, d_ff_7_q};  // Bit_Extender bit_extender_2

  // Notes on the sheet:
  //   Emergency
  //   Normal
  //   Patient queue (push value at current index)
  //   Patient Confirm
  //   (for incrementing index)
  //   Patient queue (push value at current index)
  //   Turn on clock  with 1khz
  //   Emergency Queue
  //   Normal Queue
  //   When Q is empty Doctor confirm still does decrese index
  //   When Q is full Patient confirm still increse index
  //   Doctor Select
endmodule

module _4_2 (
  input  a,
  input  b,
  input  c,
  input  d,
  output x,
  output y
);

  wire and_1_out, and_2_out, and_3_out, and_4_out, not_1_out, not_2_out, not_3_out, not_4_out, not_5_out,
       not_6_out, not_7_out, not_8_out, not_9_out, not_10_out, not_11_out, not_12_out;

  not not_1 (not_1_out, a);
  not not_2 (not_2_out, b);
  not not_3 (not_3_out, d);
  not not_4 (not_4_out, a);
  not not_5 (not_5_out, c);
  not not_6 (not_6_out, d);
  not not_7 (not_7_out, a);
  not not_8 (not_8_out, b);
  not not_9 (not_9_out, d);
  not not_10 (not_10_out, b);
  not not_11 (not_11_out, c);
  not not_12 (not_12_out, d);
  and and_1 (and_1_out, not_1_out, not_2_out, c, not_3_out);
  or or_1 (x, and_1_out, and_2_out);
  and and_2 (and_2_out, not_4_out, b, not_5_out, not_6_out);
  and and_3 (and_3_out, not_7_out, not_8_out, c, not_9_out);
  or or_2 (y, and_3_out, and_4_out);
  and and_4 (and_4_out, a, not_10_out, not_11_out, not_12_out);
endmodule
