// Logisim project time delay.circ as structural Verilog: 2 circuits, main circuit test
module test (
  input  in_1,
  output out_2
);

  _4_sec_delay u_4_sec_delay_1 (.Start(in_1), .Output(out_2));
endmodule

module _4_sec_delay (
  input  Start,
  output Output
);

  wire clock_1_out, counter_1_carry, multiplexer_1_out;

  Counter #(.width(11), .max('h6ff)) counter_1 (
    .carry(counter_1_carry), .clk(multiplexer_1_out), .clr(Start));  // open: load, D, count, Q
  Multiplexer #(.enable("false")) multiplexer_1 (
    .in1(clock_1_out), .out(multiplexer_1_out), .sel(Output));  // open: in0
  Clock clock_1 (.out(clock_1_out));
  not not_1 (Output, counter_1_carry);

  // Notes on the sheet:
  //   Send 1 to Start then get 1 for 4 Clock durations at the output
endmodule
